# Fritzing sketch Pi Hat (saved by Fritzing 0.9.4)
circuit board: 8.53488cm x 5.63626cm
breadboards: 1

parts:
  Raspberry_Pi_1 = Raspberry Pi 3 [part_number=RPI-3-V1.2]
  Part1 = Adafruit TB6612 DC and Stepper Motor Driver [part_number="Adafruit #2448"]
  J1 = screw terminal, 4 pins
  PWR_IN = Screw terminal - 2 pins [package=THT]
  U1 = Voltage Regulator - 5V [package="TO220 [THT]"]
  Pad1 = Pad [width=17.82241585707693 height=15.911189737141724 connect=center]  # not connected

nets:
  3V3: Raspberry_Pi_1.3v3, Raspberry_Pi_1.3V3, Part1.VCC, Part1.PWMB, Part1.PWMA
  N1: Raspberry_Pi_1.GPIO5, Part1.AIN2
  N2: Raspberry_Pi_1.GPIO6, Part1.AIN1
  N3: Raspberry_Pi_1.GPIO13, Part1.STBY
  N4: Raspberry_Pi_1.GPIO19, Part1.BIN1
  N5: Raspberry_Pi_1.GPIO26, Part1.BIN2
  N6: Raspberry_Pi_1.5V, U1.output_voltage
  N7: Part1.Vmotor, Part1.PWRIN, PWR_IN.pin1, U1.input_voltage
  N8: Part1.MOTORA1, J1.pin1
  N9: Part1.MOTORA2, J1.pin2
  N10: Part1.MOTORB2, J1.pin3
  N11: Part1.MOTORB1, J1.pin4

notes:
  M1
  M2
  PiBot Control Board v1
  Designed by J M Sams

custom parts:
  Adafruit TB6612 DC and Stepper Motor Driver: Spin two DC motors, step one bi-polar or uni-polar stepper, or fire off two solenoids with 1.2A per channel using the TB6612. These are perhaps better known as "the drivers in our assembled Adafruit Motorshield or Motor HAT." We really like these dual H-bridges, so if you want to control motors without a shield or HAT these are easy to include on any solderless breadboard or perma-proto.
